# Fritzing sketch AirLogger (saved by Fritzing 0.9.3b)

parts:
  DC-DC_step-up_converter_@5V = DC-DC 5V step-up [chip_label="DC-DC 5V step-up" package="DIP (Dual Inline) [THT]"]
  Lithium_battery = LIPO-110mAh [package=lipo-110]
  MicroSD_module = MicroSD Card Module
  Arduino_Pro_Mini_ATmega328P_3_3V_8MHz = Arduino Pro Mini (3.3V)
  PMS5003 = double row female pin header, 8 pins [form="♀ (female)"]
  BME280 = Barometric Pressure Sensor - BMP180 Breakout (GY-68)

nets:
  N1: DC-DC_step-up_converter_@5V.IN+, Lithium_battery.+
  N2: DC-DC_step-up_converter_@5V.IN-, Lithium_battery.-
  GND: DC-DC_step-up_converter_@5V.GND, MicroSD_module.GND, Arduino_Pro_Mini_ATmega328P_3_3V_8MHz.GND, PMS5003.pin2, BME280.GND
  VCC: DC-DC_step-up_converter_@5V.5V, MicroSD_module.VCC, Arduino_Pro_Mini_ATmega328P_3_3V_8MHz.RAW, PMS5003.pin1, BME280.VCC
  N3: MicroSD_module.MISO, Arduino_Pro_Mini_ATmega328P_3_3V_8MHz.MISO
  N4: MicroSD_module.MOSI, Arduino_Pro_Mini_ATmega328P_3_3V_8MHz.MOSI
  N5: MicroSD_module.SCK, Arduino_Pro_Mini_ATmega328P_3_3V_8MHz.SCK
  N6: MicroSD_module.CS, Arduino_Pro_Mini_ATmega328P_3_3V_8MHz.D10
  N7: Arduino_Pro_Mini_ATmega328P_3_3V_8MHz.A4, BME280.SDA
  N8: Arduino_Pro_Mini_ATmega328P_3_3V_8MHz.A5, BME280.SCL
  N9: Arduino_Pro_Mini_ATmega328P_3_3V_8MHz.D3, PMS5003.pin4
  N10: Arduino_Pro_Mini_ATmega328P_3_3V_8MHz.D2, PMS5003.pin5

custom parts:
  DC-DC 5V step-up: Повышающий модуль постоянного напряжения
